# Fritzing sketch arduino-mockup (saved by Fritzing 0.9.0b)
breadboards: 1

parts:
  Composant1 = Arduino Uno (Rev3)
  IR1 = TSOP312.., 314.. [package=THT]
  R1 = Resistor [package="2010 [SMD]"]
  D1 = LTE-302 [package=lte-302]

nets:
  N1: Composant1.D11_PWM/MOSI, IR1.Data
  N2: Composant1.D3_PWM, R1.Pin_1
  N3: Composant1.5V, IR1.Vs
  GND: Composant1.GND, IR1.GND, D1.C
  N4: R1.Pin_0, D1.A
